# Fritzing sketch LED (saved by Fritzing 0.9.3b)
breadboards: 1

parts:
  Part1 = Arduino Mega 2560 (Rev3)
  R1 = Resistor [tolerance=±5% resistance=330 package="0402 [SMD]"]
  LED1 = LED - 3mm [color="Red (633nm)" package="3 mm [THT]"]
  LED2 = LED - 3mm [color="Red (633nm)" package="3 mm [THT]"]
  LED3 = LED - 3mm [color="Red (633nm)" package="3 mm [THT]"]

nets:
  N1: Part1.5V, R1.Pin_0
  N2: Part1.D52, LED1.cathode, LED2.cathode, LED3.cathode
  N3: R1.Pin_1, LED1.anode, LED2.anode, LED3.anode

// code stored in the sketch: Untitled2.ino

